# Fritzing sketch circuit (saved by Fritzing 0.9.3b)
breadboards: 1

parts:
  U1 = ESP32S-HiLetgo [part_number=ESP32S-HiLetgo]
  U2 = 74HC04_HEX_INVERTER [package=dil14]
  IR1 = tl1838 [package=THT]
  LED1 = LED - 3mm [color="Blue (470nm)" package="3 mm [THT]"]
  R1 = Resistor [tolerance=±5% resistance=470 package=THT]
  LED2 = LED - 5mm [color="Infrared (940nm)" package="5 mm [THT]"]
  R2 = Resistor [tolerance=±5% resistance=470 package=THT]

nets:
  IR_RX: U1.GPIO39, U2.1Y, LED1.anode
  GND: U1.GND, U2.GND, IR1.GND, R1.Pin_0, R2.Pin_1
  5V: U1.VIN, U2.VCC
  IR_TX: U1.GPIO16, LED2.anode
  N1: U2.1A, IR1.OUT
  3.3V: IR1.VCC
  N2: LED1.cathode, R1.Pin_1
  N3: LED2.cathode, R2.Pin_0

notes:
  IR Tx-Rx test circuit

custom parts:
  ESP32S-HiLetgo: HiLetgo ESP-WROOM-32 ESP32 ESP-32S Development Board 2.4GHz Dual-Mode WiFi + Bluetooth Dual Cores Microcontroller The ESP32 integrated with Antenna switches, RF Balun, power amplifiers, low-noise amplifiers, filters, and management modules, and the entire solution occupies the least area of PCB. 2.4 GHz Wi-Fi plus Bluetooth dual-mode chip, with TSMC Ultra-low power consumption 40nm technology,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
  tl1838: The TL1838 is a miniaturized receiver for infrared remote control systems. A PIN diode and a preamplifier are assembled on a lead frame, the epoxy package acts as an IR filter. The demodulated output signal can be directly decoded by a microprocessor.
